# Fritzing sketch RC_ITI_First_Project (saved by Fritzing 0.9.10b)
breadboards: 1

parts:
  Part1 = Arduino Uno (Rev3)
  L298N1 = L298N DC motor driver
  S1 = Pushbutton [package="[THT]"]
  M1 = gear-motor
  M2 = gear-motor  # not connected
  M3 = gear-motor  # not connected
  M4 = gear-motor
  Part2 = Bluetooth HC-05 Macho
  HC-SR04_Sensor_1 = HC-SR04 Ultrasonic Distance Sensor
  J1 = Basic Servo
  M5 = fc-51 [package=THT]
  M6 = fc-51 [package=THT]
  M7 = fc-51 [package=THT]

nets:
  N1: Part1.A3, M7.pin1
  N2: Part1.A4/SDA, HC-SR04_Sensor_1.ECHO
  N3: Part1.A5/SCL, HC-SR04_Sensor_1.TRIG
  N4: Part1.D8, L298N1.IN3
  N5: Part1.D9_PWM, J1.pulse
  N6: Part1.D10_PWM/SS, M5.pin1
  N7: Part1.D11_PWM/MOSI, L298N1.ENA
  N8: Part1.D12/MISO, L298N1.IN2
  N9: Part1.D13/SCK, L298N1.IN1
  GND: Part1.GND, L298N1.GND, Part2.GND, J1.gnd, M5.pin2, M6.pin2
  VCC: Part1.D2, Part1.5V, S1.Pin_3, S1.Pin_4, Part2.VCC, J1.vcc, M5.pin3, M6.pin3
  N10: Part1.D3_PWM, Part2.TXD
  N11: Part1.D4, Part2.RXD
  N12: Part1.D5_PWM, M6.pin1
  N13: Part1.D6_PWM, L298N1.ENB
  N14: Part1.D7, L298N1.IN4
  N15: L298N1.OUT1, M1.pin_2
  N16: L298N1.OUT2, M1.pin_1
  N17: L298N1.OUT3, M4.pin_2
  N18: L298N1.OUT4, M4.pin_1
  N19: S1.Pin_1, S1.Pin_2

custom parts:
  L298N DC motor driver: 2x DC motor driver with 78M05 positive voltage regulator (7..35 V) L298N: max 46 V, 2 A Set 5 V Enable jumper to enable 5 V regultor (needed for the L298N) and +5 V output at screw terminal or supply external +5 V at screw terminal Set ENA and/or ENB to +5 V to enable motor permanently or supply ENA and/or ENB with PWM signal IN1 and IN2 set rotation directory for motor A (OUT1/OUT2) IN2 and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
